# Fritzing sketch Autonomous Cockroach (saved by Fritzing 0.9.2b)
breadboards: 1

parts:
  Part1 = Arduino Uno (Rev3)
  IC1 = L293D [package=THT]
  VCC1 = Battery block 9V
  Servo = Header 4 [package=jst-4-pth]
  Motor = Header 4 [package=jst-4-pth]
  R1 = Resistor [tolerance=±5% resistance=10k package="0402 [SMD]"]
  R2 = Resistor [tolerance=±5% resistance=10k package="0402 [SMD]"]
  R3 = Photocell (LDR) [package=THT]
  R4 = Photocell (LDR) [package=THT]

nets:
  N1: Part1.A0, R1.Pin_0, R3.pin_0
  N2: Part1.A1, R2.Pin_0, R4.pin_0
  N3: Part1.D9_PWM, IC1.In_1
  N4: Part1.D10_PWM/SS, IC1.In_3
  N5: Part1.D11_PWM/MOSI, IC1.In_4
  N6: Part1.D3_PWM, IC1.In_2
  N7: Part1.5V, IC1.+V, R3.pin_1, R4.pin_1
  N8: Part1.GND, IC1.0V, VCC1.-, Servo.4, Motor.4, R1.Pin_1, R2.Pin_1
  N9: Part1.VIN, IC1.+Vmotor, VCC1.+, Servo.1, Motor.1
  N10: IC1.Out_1_(_Controlled_by_Enable_1_), Servo.2
  N11: IC1.Out_2_(_Controlled_by_Enable_1_), Servo.3
  N12: IC1.Out_3_(_Controlled_by_Enable_2_), Motor.3
  N13: IC1.Out_4_(_Controlled_by_Enable_2_), Motor.2
